# Fritzing sketch smister (saved by Fritzing 1.0.5)
breadboards: 1

parts:
  Mod1 = Raspberry Pi 4B
  Power_plug1 = Power plug
  J1 = Basic Servo
  J2 = Basic Servo
  J3 = Basic Servo
  K1 = Relay [part_number=FRS1B-S package=THT]
  M1 = DC Motor [voltage_(max)=6V voltage_(min)=3V]
  HC-SR04_Sensor_1 = HC-SR04 Ultrasonic Distance Sensor
  HC-SR04_Sensor_2 = HC-SR04 Ultrasonic Distance Sensor
  HC-SR04_Sensor_3 = HC-SR04 Ultrasonic Distance Sensor

nets:
  VCC: Mod1.5V, J1.vcc, J2.vcc, J3.vcc, HC-SR04_Sensor_1.VCC, HC-SR04_Sensor_2.VCC, HC-SR04_Sensor_3.VCC
  GND: Mod1.GND, J1.gnd, J2.gnd, J3.gnd, K1.COIL2, M1.pin_1, HC-SR04_Sensor_1.GND, HC-SR04_Sensor_2.GND, HC-SR04_Sensor_3.GND
  N1: Mod1.GPIO14, HC-SR04_Sensor_1.ECHO
  N2: Mod1.GPIO15, HC-SR04_Sensor_2.ECHO
  N3: Mod1.GPIO18, HC-SR04_Sensor_3.ECHO
  N4: Mod1.GPIO25, HC-SR04_Sensor_1.TRIG
  N5: Mod1.GPIO8, HC-SR04_Sensor_2.TRIG
  N6: Mod1.GPIO7, HC-SR04_Sensor_3.TRIG
  N7: Mod1.GPIO12, J1.pulse
  N8: Mod1.GPIO13, J2.pulse
  N9: Mod1.GPIO16, J3.pulse
  N10: Mod1.GPIO21, K1.COIL1
  N11: Power_plug1.VCC, K1.C1, K1.C2
  N12: Power_plug1.GND, K1.A
  N13: K1.B, M1.pin_2
